// Digital circuit alu.dig as structural Verilog
module alu (
  input  [3:0] AluOp,
  input  [15:0] Rhs,
  input  [15:0] Lhs,
  input  [2:0] JmpCond,
  output [15:0] Result
);

  wire multiplexer_2_out;
  wire [15:0] add_1_s, and_1_out, asr_out, lsr_out, multiplexer_1_out, multiplexer_3_out, multiplexer_4_out,
       neg_1_out, not_1_out, or_1_out, shl_out, xor_1_out;

  Neg #(.Bits(16)) neg_1 (.in(Rhs), .out(neg_1_out));
  Multiplexer #(.Bits(16)) multiplexer_1 (.sel(AluOp[3]), .in_0(Rhs), .in_1(neg_1_out), .out(multiplexer_1_out));
  assign and_1_out = Lhs & Rhs;  // And and_1, 16 bits wide
  assign or_1_out = Lhs | Rhs;  // Or or_1, 16 bits wide
  assign xor_1_out = Lhs ^ Rhs;  // XOr xor_1, 16 bits wide
  assign not_1_out = ~Rhs;  // Not not_1, 16 bits wide
  Multiplexer multiplexer_2 (.sel(AluOp[0]), .in_0(1'b0), .in_1(1'b1), .out(multiplexer_2_out));
  BarrelShifter #(.Bits(16)) shl (.in(Lhs), .shift(Rhs[4:0]), .out(shl_out));
  BarrelShifter #(.Bits(16), .direction("right")) lsr (.in(Lhs), .shift(Rhs[4:0]), .out(lsr_out));
  BarrelShifter #(.Bits(16), .barrelShifterMode("arithmetic"), .direction("right")) asr (
    .in(Lhs), .shift(Rhs[4:0]), .out(asr_out));
  Add #(.Bits(16)) add_1 (.a(Lhs), .b(multiplexer_1_out), .c_i(multiplexer_2_out), .s(add_1_s));  // open: c_o
  Multiplexer #(.Selector_Bits(2), .Bits(16)) multiplexer_3 (
    .sel(AluOp[1:0]), .in_0(and_1_out), .in_1(or_1_out), .in_2(xor_1_out), .in_3(not_1_out),
    .out(multiplexer_3_out));
  Multiplexer #(.Selector_Bits(2), .Bits(16)) multiplexer_4 (
    .sel(AluOp[1:0]), .in_0({Rhs[7:0], Rhs[15:8]}), .in_1(shl_out), .in_2(lsr_out), .in_3(asr_out),
    .out(multiplexer_4_out));
  Multiplexer #(.Selector_Bits(2), .Bits(16)) multiplexer_5 (
    .sel(AluOp[3:2]), .in_0(multiplexer_3_out), .in_1(add_1_s), .in_2(add_1_s), .in_3(multiplexer_4_out),
    .out(Result));
endmodule
