// Digital circuit cpu.dig as structural Verilog
module cpu (
  input  clk
);

  wire decode_1_leftsel, decode_1_rightsel;
  wire [1:0] decode_1_writebackmode, Decode_Execute_wrbacken_2, Execute_Memory_wrbacken_2,
       Memory_Writeback_p5;
  wire [2:0] decode_1_jmpcond, decode_1_memorymode, Decode_Execute_jmpcond_2, Decode_Execute_memmode_2,
       Execute_Memory_memmode_2;
  wire [3:0] decode_1_alufunc, decode_1_destreg, decode_1_srcreg, Decode_Execute_aluop_2;
  wire [15:0] alu_1_result, decode_1_imm, Decode_Execute_datasrc_2, Decode_Execute_lhs_2,
       Decode_Execute_rhs_2, Execute_Memory_alures_2, Execute_Memory_datasrc_2, fetch_1_inst,
       fetch_1_progcount, Fetch_Decode_inst_2, mem_1_q, Memory_Writeback_p6, Memory_Writeback_p7,
       multiplexer_1_out, RegFile_datasrc, RegFile_lhs, RegFile_rhs;

  fetch fetch_1 (
    .FetchEn(1'b1), .JmpEn(1'b1), .JmpDst(mem_1_q), .clk(clk), .Mem(mem_1_q), .Inst(fetch_1_inst),
    .ProgCount(fetch_1_progcount));
  f_de Fetch_Decode (.Inst(fetch_1_inst), .clk(clk), .Inst_2(Fetch_Decode_inst_2));
  decode decode_1 (
    .Inst(Fetch_Decode_inst_2), .clk(clk), .WritebackMode(decode_1_writebackmode),
    .MemoryMode(decode_1_memorymode), .JmpCond(decode_1_jmpcond), .AluFunc(decode_1_alufunc),
    .RightSel(decode_1_rightsel), .LeftSel(decode_1_leftsel), .Imm(decode_1_imm), .DestReg(decode_1_destreg),
    .SrcReg(decode_1_srcreg));
  operands RegFile (
    .RSel(decode_1_rightsel), .LSel(decode_1_leftsel), .Imm(decode_1_imm), .RegB(decode_1_destreg),
    .RegA(decode_1_srcreg), .clk(clk), .ProgCt(fetch_1_progcount), .WrEn(Memory_Writeback_p5[1]),
    .DataIn(multiplexer_1_out), .Rhs(RegFile_rhs), .Lhs(RegFile_lhs), .DataSrc(RegFile_datasrc));
  de_ex Decode_Execute (
    .WrBackEn(decode_1_writebackmode), .MemMode(decode_1_memorymode), .JmpCond(decode_1_jmpcond),
    .AluOp(decode_1_alufunc), .Rhs(RegFile_rhs), .Lhs(RegFile_lhs), .DataSrc(RegFile_datasrc), .clk(clk),
    .WrBackEn_2(Decode_Execute_wrbacken_2), .MemMode_2(Decode_Execute_memmode_2),
    .JmpCond_2(Decode_Execute_jmpcond_2), .AluOp_2(Decode_Execute_aluop_2), .Rhs_2(Decode_Execute_rhs_2),
    .Lhs_2(Decode_Execute_lhs_2), .DataSrc_2(Decode_Execute_datasrc_2));
  alu alu_1 (
    .JmpCond(Decode_Execute_jmpcond_2), .AluOp(Decode_Execute_aluop_2), .Rhs(Decode_Execute_rhs_2),
    .Lhs(Decode_Execute_lhs_2), .Result(alu_1_result));
  ex_mem Execute_Memory (
    .WrBackEn(Decode_Execute_wrbacken_2), .MemMode(Decode_Execute_memmode_2), .clk(clk),
    .AluRes(alu_1_result), .DataSrc(Decode_Execute_datasrc_2), .WrBackEn_2(Execute_Memory_wrbacken_2),
    .MemMode_2(Execute_Memory_memmode_2), .AluRes_2(Execute_Memory_alures_2),
    .DataSrc_2(Execute_Memory_datasrc_2));
  mem mem_1 (
    .MemMode(Execute_Memory_memmode_2), .DataIn(Execute_Memory_alures_2), .Addr(Execute_Memory_datasrc_2),
    .clk(clk), .Q(mem_1_q));
  // mem_wb Memory_Writeback: pin names not known; wires that end beside it: Execute_Memory_wrbacken_2, clk, Execute_Memory_alures_2, mem_1_q, Memory_Writeback_p5, Memory_Writeback_p6, Memory_Writeback_p7
  Multiplexer #(.Bits(16)) multiplexer_1 (
    .sel(Memory_Writeback_p5[0]), .in_0(Memory_Writeback_p6), .in_1(Memory_Writeback_p7),
    .out(multiplexer_1_out));
endmodule
