// Digital circuit de_ex.dig as structural Verilog
module de_ex (
  input  [1:0] WrBackEn,
  input  [2:0] MemMode,
  input  [2:0] JmpCond,
  input  [3:0] AluOp,
  input  [15:0] Rhs,
  input  [15:0] Lhs,
  input  [15:0] DataSrc,
  input  clk,
  output [1:0] WrBackEn_2,
  output [2:0] MemMode_2,
  output [2:0] JmpCond_2,
  output [3:0] AluOp_2,
  output [15:0] Rhs_2,
  output [15:0] Lhs_2,
  output [15:0] DataSrc_2
);

  Register #(.Bits(3)) register_1 (.D(JmpCond), .C(clk), .en(1'b1), .Q(JmpCond_2));
  Register #(.Bits(4)) register_2 (.D(AluOp), .C(clk), .en(1'b1), .Q(AluOp_2));
  Register #(.Bits(16)) register_3 (.D(Lhs), .C(clk), .en(1'b1), .Q(Lhs_2));
  Register #(.Bits(16)) register_4 (.D(Rhs), .C(clk), .en(1'b1), .Q(Rhs_2));
  Register #(.Bits(3)) register_5 (.D(MemMode), .C(clk), .en(1'b1), .Q(MemMode_2));
  Register #(.Bits(16)) register_6 (.D(DataSrc), .C(clk), .en(1'b1), .Q(DataSrc_2));
  Register #(.Bits(2)) register_7 (.D(WrBackEn), .C(clk), .en(1'b1), .Q(WrBackEn_2));
endmodule
