// Digital circuit decode.dig as structural Verilog
module decode (
  input  [15:0] Inst,
  input  clk,
  input  [15:0] DataIn,
  input  sxt_zxt,
  input  n3_sel,
  output [3:0] AluOp,
  output [3:0] RegA,
  output [3:0] RegB,
  output [15:0] Imm,
  output [15:0] lui_imm,
  output [15:0] mem8_imm,
  output [15:0] mem16_imm,
  output [15:0] shift_imm,
  output [15:0] alu_imm,
  output [15:0] j_imm,
  output [15:0] br_imm,
  output [15:0] imm_2
);

  wire nib0;

  Multiplexer multiplexer_1 (.sel(sxt_zxt), .in_0(Inst[8]), .in_1(1'b0), .out(imm_2[15]));
  Multiplexer #(.Bits(3)) multiplexer_2 (.sel(n3_sel), .in_0(Inst[14:12]), .in_1({3{imm_2[15]}}), .out(imm_2[14:12]));
  Multiplexer multiplexer_3 (.out(nib0));  // open: sel, in_0, in_1

  assign alu_imm = {{12{Inst[8]}}, Inst[2:0], Inst[3]};
  assign br_imm = {{9{Inst[8]}}, Inst[5:4], Inst[7], Inst[2:0], 1'b0};
  assign j_imm = {{12{Inst[8]}}, Inst[2:0], 1'b0};
  assign lui_imm = {Inst[8], Inst[14:9], Inst[7:4], {5{1'b0}}};
  assign mem8_imm = {{12{Inst[8]}}, Inst[11:9], Inst[12]};
  assign mem16_imm = {{12{Inst[8]}}, Inst[11:9], 1'b0};
  assign shift_imm = {{12{1'b0}}, Inst[2:0], Inst[3]};

  // Other names for the same wires on the sheet: nib3[3:0] = imm_2[15:12]; b0 = Inst[0]; b1 = Inst[1]; b2 = Inst[2];
  //   b3 = Inst[3]; b4 = Inst[4]; b5 = Inst[5]; b6 = Inst[6]; b7 = Inst[7]; b8 = Inst[8]; b9 = Inst[9];
  //   b10 = Inst[10]; b11 = Inst[11]; b12 = Inst[12]; b13 = Inst[13]; b14 = Inst[14]; b15 = Inst[15]

  // Notes on the sheet:
  //   The top bit is always
  //   zero or the sign bit,
  //   which is always b8
  //   1x 2:1 Mux
  //   The high nibble is either
  //   b12,13,14,8 or the sign/zero bit.
  //   3x 2:1 Mux
  //   jr
  //   jral
  //   br.eq
  //   br.ne
  //   br.lt
  //   br.ge
  //   br.lts
  //   br.ges
  //   lui
  //   ld8z
  //   st8
  //   ld
  //   st
  //   shli
  //   lsri
  //   asri
  //   andi
  //   ori
  //   stz
  //   irq
  //   sys
  //   env
  //   li
  //   addi
  //   cmpi
  //   j
  //   jal
endmodule
