// Digital circuit ex_mem.dig as structural Verilog
module ex_mem (
  input  MemRdEn,
  input  [1:0] MemWrEn,
  input  [1:0] WrBackEn_2,
  input  [15:0] DataSrc,
  input  clk,
  input  [15:0] AluRes,
  output [1:0] WrBackEn,
  output MemRdEn_2,
  output [1:0] MemWrEn_2,
  output [15:0] DataSrc_2,
  output [15:0] AluRes_2
);

  Register #(.Bits(16)) register_1 (.D(DataSrc), .C(clk), .en(1'b1), .Q(DataSrc_2));
  Register #(.Bits(16)) register_2 (.D(AluRes), .C(clk), .en(1'b1), .Q(AluRes_2));
  Register register_3 (.D(MemRdEn), .C(clk), .en(1'b1), .Q(MemRdEn_2));
  Register #(.Bits(2)) register_4 (.D(MemWrEn), .C(clk), .en(1'b1), .Q(MemWrEn_2));
  Register #(.Bits(2)) register_5 (.D(WrBackEn_2), .C(clk), .en(1'b1), .Q(WrBackEn));
endmodule
