// Digital circuit f_de.dig as structural Verilog
module f_de (
  input  [15:0] Inst,
  input  clk,
  output [15:0] Inst_2
);

  Register #(.Bits(16)) register_1 (.D(Inst), .C(clk), .en(1'b1), .Q(Inst_2));
endmodule
