// Digital circuit fetch.dig as structural Verilog
module fetch (
  input  [7:0] imm,
  input  clk,
  input  Load_UDS,
  input  Load_KDS
);

  wire [7:0] _16x_8b_da, _16x_8b_db, Alu_Result_2_q, ALU_s, LHS_q, Mem_Result_q, multiplexer_2_out,
       multiplexer_3_out, multiplexer_4_out, multiplexer_5_out, RHS_q;
  wire [7:1] undriven;
  wire [15:0] Addr_Base_q, Addr_Index_q, Addr_Result_2_q, Addr_Result_q, Alu_Result_q, bitextender_1_out,
       DS_q, KDS_q, logical_s, multiplexer_1_out, ramdualport_1_d, Segment_q;
  wire [23:0] MAR_q, physical_s;

  RegisterFile #(.AddrBits(4), .Bits(8)) _16x_8b (
    .Din(multiplexer_5_out), .C(clk), .Da(_16x_8b_da), .Db(_16x_8b_db));  // open: we, Rw, Ra, Rb
  Register #(.Bits(16)) DS (.D(Addr_Result_2_q), .C(clk), .en(Load_UDS), .Q(DS_q));
  Register #(.Bits(16)) KDS (.D(Addr_Result_2_q), .C(clk), .en(Load_KDS), .Q(KDS_q));
  Multiplexer #(.Bits(16)) multiplexer_1 (.sel(1'b0), .in_0(DS_q), .in_1(KDS_q), .out(multiplexer_1_out));
  BitExtender bitextender_1 (.in(imm), .out(bitextender_1_out));
  Multiplexer multiplexer_2 (.sel(1'b0), .in_0(_16x_8b_db[0]), .in_1(imm[0]), .out(multiplexer_2_out[0]));
  Register #(.Bits(16)) Segment (.D(multiplexer_1_out), .C(clk), .Q(Segment_q));  // open: en
  Register #(.Bits(16)) Addr_Base (.D({_16x_8b_db, _16x_8b_da}), .C(clk), .Q(Addr_Base_q));  // open: en
  Register #(.Bits(16)) Addr_Index (.D(bitextender_1_out), .C(clk), .Q(Addr_Index_q));  // open: en
  Register #(.Bits(8)) LHS (.D(_16x_8b_da), .C(clk), .Q(LHS_q));  // open: en
  Register #(.Bits(8)) RHS (.D(multiplexer_2_out), .C(clk), .Q(RHS_q));  // open: en
  Add #(.Bits(16)) logical (.a(Addr_Base_q), .b(Addr_Index_q), .c_i(1'b0), .s(logical_s));  // open: c_o
  Add #(.Bits(8)) ALU (.a(LHS_q), .b(RHS_q), .c_i(1'b0), .s(ALU_s));  // open: c_o
  Multiplexer multiplexer_3 (.sel(1'b0), .in_0(ALU_s[0]), .in_1(imm[0]), .out(multiplexer_3_out[0]));
  Add #(.Bits(24)) physical (
    .a({{8{1'b0}}, logical_s}), .b({Segment_q, undriven, 1'b0}), .c_i(1'b0), .s(physical_s));  // open: c_o
  Register #(.Bits(16)) Addr_Result (.D(logical_s), .C(clk), .Q(Addr_Result_q));  // open: en
  Register #(.Bits(24)) MAR (.D(physical_s), .C(clk), .Q(MAR_q));  // open: en
  Register #(.Bits(8)) Alu_Result (.D(multiplexer_3_out), .C(clk), .Q(Alu_Result_q[7:0]));  // open: en
  RAMDualPort #(.AddrBits(24), .Bits(16)) ramdualport_1 (
    .A(MAR_q), .Din(Alu_Result_q), .C(clk), .D(ramdualport_1_d));  // open: str, ld
  Multiplexer multiplexer_4 (
    .sel(MAR_q[0]), .in_0(ramdualport_1_d[0]), .in_1(ramdualport_1_d[8]), .out(multiplexer_4_out[0]));
  Register #(.Bits(16)) Addr_Result_2 (.D(Addr_Result_q), .C(clk), .Q(Addr_Result_2_q));  // open: en
  Register #(.Bits(8)) Mem_Result (.D(multiplexer_4_out), .C(clk), .Q(Mem_Result_q));  // open: en
  Register #(.Bits(8)) Alu_Result_2 (.D(Alu_Result_q[7:0]), .C(clk), .Q(Alu_Result_2_q));  // open: en
  Multiplexer multiplexer_5 (
    .in_0(Mem_Result_q[0]), .in_1(Alu_Result_2_q[0]), .out(multiplexer_5_out[0]));  // open: sel
  // Pins of 1 and 8 bits meet at multiplexer_5_out
  // Pins of 1 and 8 bits meet at _16x_8b_db
  // Pins of 1 and 8 bits meet at ALU_s
  // Pins of 1 and 8 bits meet at imm
  // Pins of 1 and 8 bits meet at multiplexer_2_out
  // Pins of 1 and 8 bits meet at multiplexer_3_out
  // Pins of 8 and 16 bits meet at Alu_Result_q
  // Pins of 1 and 8 bits meet at {undriven, 1'b0}
  // Pins of 1 and 8 bits meet at multiplexer_4_out
  // Pins of 1 and 8 bits meet at Mem_Result_q
  // Pins of 1 and 8 bits meet at Alu_Result_2_q
  // Pins of 1 and 8 bits meet at ramdualport_1_d[7:0]

  // Notes on the sheet:
  //   Decode
  //   Execute
  //   Memory
  //   Writeback
endmodule
