// Digital circuit mem.dig as structural Verilog
module mem (
  input  MemRdEn,
  input  [1:0] MemWrEn,
  input  [15:0] DataIn,
  input  [15:0] Addr,
  input  clk,
  output [15:0] Q
);

  wire byte_word, sxt_zxt;
  wire [7:0] multiplexer_1_out, rom_1_d, rom_2_d;
  wire [15:0] bitextender_1_out, multiplexer_2_out;

  ROM #(.AddrBits(15), .Bits(8)) rom_1 (.A(Addr[14:0]), .sel(1'b1), .D(rom_1_d));
  ROM #(.AddrBits(15), .Bits(8)) rom_2 (.A(Addr[14:0]), .sel(1'b1), .D(rom_2_d));
  Multiplexer #(.Bits(8)) multiplexer_1 (.sel(Addr[15]), .in_0(rom_1_d), .in_1(rom_2_d), .out(multiplexer_1_out));
  BitExtender bitextender_1 (.in(multiplexer_1_out), .out(bitextender_1_out));
  Multiplexer #(.Bits(16)) multiplexer_2 (
    .sel(sxt_zxt), .in_0(bitextender_1_out), .in_1({{8{1'b0}}, multiplexer_1_out}), .out(multiplexer_2_out));
  Multiplexer #(.Bits(16)) multiplexer_3 (
    .sel(byte_word), .in_0(multiplexer_2_out), .in_1({rom_2_d, rom_1_d}), .out(Q));
endmodule
