// Digital circuit mem_wb.dig as structural Verilog
module mem_wb (
  input  [1:0] WrBackEn,
  input  clk,
  input  [15:0] AluRes,
  input  [15:0] MemRes_2,
  output [1:0] WrBackEn_2,
  output [15:0] MemRes,
  output [15:0] AluRes_2
);

  Register #(.Bits(2)) register_1 (.D(WrBackEn), .C(clk), .en(1'b1), .Q(WrBackEn_2));
  Register #(.Bits(16)) register_2 (.D(AluRes), .C(clk), .en(1'b1), .Q(AluRes_2));
  Register #(.Bits(16)) register_3 (.D(MemRes_2), .C(clk), .en(1'b1), .Q(MemRes));
endmodule
