// Digital circuit mmu.dig as structural Verilog
module mmu (
  input  [15:0] virt_addr,
  input  code_ndata,
  input  read_nwrite,
  output [20:0] phy_addr,
  output access_violation_fault,
  output read_nwrite_2
);

  wire [1:0] multiplexer_1_out;
  wire [3:3] undriven;
  wire [7:0] MMU_d;

  ROM #(.AddrBits(4), .Bits(16)) MMU (.A({code_ndata, virt_addr[15:13]}), .sel(1'b1), .D({phy_addr[20:13], MMU_d}));
  Multiplexer #(.Bits(2), .Selector_Bits(2)) multiplexer_1 (
    .sel(virt_addr[11:10]), .in_0(MMU_d[1:0]), .in_1(MMU_d[3:2]), .in_2(MMU_d[5:4]), .in_3(MMU_d[7:6]),
    .out(multiplexer_1_out));
  Multiplexer multiplexer_2 (
    .sel(read_nwrite), .in_0(multiplexer_1_out[0]), .in_1(multiplexer_1_out[1]), .out(access_violation_fault));
  // Pins of 2 and 4 bits meet at {undriven[3], virt_addr[12:10]}

  assign phy_addr[12:0] = virt_addr[12:0];
  assign read_nwrite_2 = read_nwrite;
endmodule
