// Digital circuit operands.dig as structural Verilog
module operands (
  input  RSel,
  input  LSel,
  input  [15:0] Imm,
  input  [3:0] RegB,
  input  [3:0] RegA,
  input  clk,
  input  [15:0] ProgCt,
  input  WrEn,
  input  [15:0] DataIn,
  output [15:0] Rhs,
  output [15:0] Lhs,
  output [15:0] DataSrc
);

  wire [15:0] registerfile_1_da;

  RegisterFile #(.AddrBits(4), .Bits(16)) registerfile_1 (
    .Din(DataIn), .we(WrEn), .Rw(RegA), .C(clk), .Ra(RegA), .Rb(RegB), .Da(registerfile_1_da), .Db(DataSrc));
  Multiplexer #(.Bits(16)) multiplexer_1 (.sel(LSel), .in_0(ProgCt), .in_1(registerfile_1_da), .out(Lhs));
  Multiplexer #(.Bits(16)) multiplexer_2 (.sel(RSel), .in_0(DataSrc), .in_1(Imm), .out(Rhs));
endmodule
