// Digital circuit pc.dig as structural Verilog
module pc (
  input  clk,
  input  fetch,
  input  [15:0] addr,
  input  jmp_en,
  output [15:0] Q
);

  wire [15:0] add_1_s, multiplexer_1_out;

  Register #(.Bits(16)) register_1 (.D(multiplexer_1_out), .C(clk), .en(fetch), .Q(Q));
  Multiplexer #(.Bits(16)) multiplexer_1 (.sel(jmp_en), .in_0(add_1_s), .in_1(addr), .out(multiplexer_1_out));
  Add #(.Bits(16)) add_1 (.a(16'h2), .b(Q), .c_i(1'b0), .s(add_1_s));  // open: c_o

  // Notes on the sheet:
  //   fetch: When active, increments the Program Counter
  //   by 2, or loads the value on the addr input
  //   if jmp-en is active.
  //   addr: Input data source to load into Program Counter
  //   when jmp-en is active.
  //   jmp_en: Jump Enable. When active, load addr into the
  //   Program Counter to jump to new execution point.
  //   Q: The stored Program Counter value.
endmodule
