// Digital circuit regfile.dig as structural Verilog
module regfile (
  input  [7:0] in,
  input  [2:0] l_sel,
  input  [2:0] r_sel,
  input  [2:0] wr_sel,
  input  wr_en,
  input  clk,
  output [7:0] left,
  output [7:0] right
);

  wire and_1_out, and_2_out, and_3_out, and_4_out, and_5_out, and_6_out, and_7_out, and_8_out,
       decoder_1_out_0, decoder_1_out_1, decoder_1_out_2, decoder_1_out_3, decoder_1_out_4, decoder_1_out_5,
       decoder_1_out_6, decoder_1_out_7;
  wire [7:0] r0_q, r1_q, r2_q, r3_q, r4_q, r5_q, r6_q, r7_q;

  Decoder #(.Selector_Bits(3)) decoder_1 (
    .sel(wr_sel), .out_0(decoder_1_out_0), .out_1(decoder_1_out_1), .out_2(decoder_1_out_2),
    .out_3(decoder_1_out_3), .out_4(decoder_1_out_4), .out_5(decoder_1_out_5), .out_6(decoder_1_out_6),
    .out_7(decoder_1_out_7));
  and and_1 (and_1_out, decoder_1_out_0, wr_en);
  and and_2 (and_2_out, decoder_1_out_1, wr_en);
  and and_3 (and_3_out, decoder_1_out_2, wr_en);
  and and_4 (and_4_out, decoder_1_out_3, wr_en);
  and and_5 (and_5_out, decoder_1_out_4, wr_en);
  and and_6 (and_6_out, decoder_1_out_5, wr_en);
  and and_7 (and_7_out, decoder_1_out_6, wr_en);
  and and_8 (and_8_out, decoder_1_out_7, wr_en);
  Register #(.Bits(8)) r0 (.D(in), .C(clk), .en(and_1_out), .Q(r0_q));
  Register #(.Bits(8)) r2 (.D(in), .C(clk), .en(and_3_out), .Q(r2_q));
  Register #(.Bits(8)) r4 (.D(in), .C(clk), .en(and_5_out), .Q(r4_q));
  Register #(.Bits(8)) r6 (.D(in), .C(clk), .en(and_7_out), .Q(r6_q));
  // Probe on r0_q
  Register #(.Bits(8)) r1 (.D(in), .C(clk), .en(and_2_out), .Q(r1_q));
  // Probe on r2_q
  Register #(.Bits(8)) r3 (.D(in), .C(clk), .en(and_4_out), .Q(r3_q));
  // Probe on r4_q
  Register #(.Bits(8)) r5 (.D(in), .C(clk), .en(and_6_out), .Q(r5_q));
  // Probe on r6_q
  Register #(.Bits(8)) r7 (.D(in), .C(clk), .en(and_8_out), .Q(r7_q));
  // Probe on r1_q
  // Probe on r3_q
  // Probe on r5_q
  // Probe on r7_q
  Multiplexer #(.Selector_Bits(3), .Bits(8)) multiplexer_1 (
    .sel(l_sel), .in_0(r0_q), .in_1(r1_q), .in_2(r2_q), .in_3(r3_q), .in_4(r4_q), .in_5(r5_q), .in_6(r6_q),
    .in_7(r7_q), .out(left));
  Multiplexer #(.Selector_Bits(3), .Bits(8)) multiplexer_2 (
    .sel(r_sel), .in_0(r0_q), .in_1(r1_q), .in_2(r2_q), .in_3(r3_q), .in_4(r4_q), .in_5(r5_q), .in_6(r6_q),
    .in_7(r7_q), .out(right));
endmodule
