// Digital circuit segfile.dig as structural Verilog
module segfile (
  input  [15:0] in,
  input  [1:0] seg_sel,
  input  [1:0] wr_sel,
  input  wr_en,
  input  clk,
  output [15:0] seg
);

  wire and_1_out, and_2_out, and_3_out, and_4_out, decoder_1_out_0, decoder_1_out_1, decoder_1_out_2,
       decoder_1_out_3;
  wire [15:0] seg0_q, seg1_q, seg2_q, seg3_q;

  Decoder #(.Selector_Bits(2)) decoder_1 (
    .sel(wr_sel), .out_0(decoder_1_out_0), .out_1(decoder_1_out_1), .out_2(decoder_1_out_2),
    .out_3(decoder_1_out_3));
  and and_1 (and_1_out, decoder_1_out_0, wr_en);
  and and_2 (and_2_out, decoder_1_out_1, wr_en);
  and and_3 (and_3_out, decoder_1_out_2, wr_en);
  and and_4 (and_4_out, decoder_1_out_3, wr_en);
  Register #(.Bits(16)) seg0 (.D(in), .C(clk), .en(and_1_out), .Q(seg0_q));
  Register #(.Bits(16)) seg1 (.D(in), .C(clk), .en(and_2_out), .Q(seg1_q));
  Register #(.Bits(16)) seg2 (.D(in), .C(clk), .en(and_3_out), .Q(seg2_q));
  Register #(.Bits(16)) seg3 (.D(in), .C(clk), .en(and_4_out), .Q(seg3_q));
  Multiplexer #(.Bits(16), .Selector_Bits(2)) multiplexer_1 (
    .sel(seg_sel), .in_0(seg0_q), .in_1(seg1_q), .in_2(seg2_q), .in_3(seg3_q), .out(seg));
  // Pins of 1 and 2 bits meet at wr_sel
endmodule
