// Digital circuit stall.dig as structural Verilog
module stall (
  input  clk,
  input  [15:0] NOP,
  input  [15:0] NOP_2,
  input  [15:0] NOP_3,
  input  [15:0] NOP_4,
  input  STALL,
  input  STOMP
);

  wire and_1_out, and_2_out, and_3_out, and_4_out, comparator_1_eq, comparator_2_eq, comparator_3_eq,
       comparator_4_eq, comparator_5_eq, comparator_6_eq, ID_EX_J_TYPE, IF_ID_J_TYPE, JUMP_HAZARD,
       MEM_HAZARD, not_1_out, not_2_out, or_1_out, or_4_out, RAW_HAZARD;
  wire [1:0] EX_MEM_MEM_MODE, EX_MEM_WR_MODE, ID_EX_WR_MODE;
  wire [3:0] DE_EX_RSRC, EX_MEM_RDST, EX_MEM_RSRC, ID_EX_RDST, IF_ID_RDST, IF_ID_RSRC;
  wire [7:0] ID_Ex_q;
  wire [14:0] add_1_s, multiplexer_3_out, register_1_q;
  wire [15:0] multiplexer_1_out, multiplexer_2_out, multiplexer_4_out, multiplexer_5_out;
  wire [15:8] Ex_Mem_q, IF_ID_q;

  Multiplexer #(.Bits(16)) multiplexer_1 (.sel(STOMP), .in_1(NOP_4), .out(multiplexer_1_out));  // open: in_0
  not not_1 (not_1_out, STALL);
  or or_1 (or_1_out, STOMP, not_1_out);
  Register #(.Bits(16)) IF_ID (.D(multiplexer_1_out), .C(clk), .en(or_1_out), .Q({IF_ID_q, IF_ID_RSRC, IF_ID_RDST}));
  Multiplexer #(.Bits(16)) multiplexer_2 (
    .sel(STOMP), .in_0({IF_ID_q, IF_ID_RSRC, IF_ID_RDST}), .in_1(NOP_3), .out(multiplexer_2_out));
  Comparator comparator_1 (.a(ID_EX_RDST[0]), .b(IF_ID_RSRC[0]), .eq(comparator_1_eq));  // open: gt, lt
  Comparator comparator_2 (.a(ID_EX_WR_MODE[0]), .b(1'b0), .eq(comparator_2_eq));  // open: gt, lt
  Comparator comparator_3 (.a(ID_EX_RDST[0]), .b(IF_ID_RDST[0]), .eq(comparator_3_eq));  // open: gt, lt
  and and_1 (and_1_out, comparator_1_eq, comparator_2_eq);
  and and_2 (and_2_out, comparator_2_eq, comparator_3_eq);
  Register #(.Bits(16)) ID_Ex (.D(multiplexer_2_out), .C(clk), .en(1'b1), .Q({ID_Ex_q, DE_EX_RSRC, ID_EX_RDST}));
  or or_2 (RAW_HAZARD, and_3_out, and_4_out, and_1_out, and_2_out);
  or or_3 (JUMP_HAZARD, ID_EX_J_TYPE, IF_ID_J_TYPE);
  nor nor_1 (MEM_HAZARD, EX_MEM_MEM_MODE[0], EX_MEM_MEM_MODE[1]);
  Comparator comparator_4 (.a(EX_MEM_RDST[0]), .b(IF_ID_RDST[0]), .eq(comparator_4_eq));  // open: gt, lt
  Comparator comparator_5 (.a(EX_MEM_WR_MODE[0]), .b(1'b0), .eq(comparator_5_eq));  // open: gt, lt
  Comparator comparator_6 (.a(EX_MEM_RDST[0]), .b(IF_ID_RDST[0]), .eq(comparator_6_eq));  // open: gt, lt
  and and_3 (and_3_out, comparator_4_eq, comparator_5_eq);
  and and_4 (and_4_out, comparator_5_eq, comparator_6_eq);
  not not_2 (not_2_out, STALL);
  or or_4 (or_4_out, not_2_out, ID_Ex_q[0]);
  Register #(.Bits(15)) register_1 (.D(multiplexer_3_out), .C(clk), .en(or_4_out), .Q(register_1_q));
  Add #(.Bits(15)) add_1 (.a(15'h1), .b(register_1_q), .c_i(1'b0), .s(add_1_s));  // open: c_o
  Multiplexer multiplexer_3 (.sel(ID_EX_J_TYPE), .in_0(add_1_s[0]), .in_1(ID_Ex_q[0]), .out(multiplexer_3_out[0]));
  Multiplexer #(.Bits(16)) multiplexer_4 (
    .in_0({ID_Ex_q, DE_EX_RSRC, ID_EX_RDST}), .in_1(NOP), .out(multiplexer_4_out));  // open: sel
  Register #(.Bits(16)) Ex_Mem (.D(multiplexer_4_out), .C(clk), .Q({Ex_Mem_q, EX_MEM_RSRC, EX_MEM_RDST}));  // open: en
  Multiplexer #(.Bits(16)) multiplexer_5 (
    .in_0({Ex_Mem_q, EX_MEM_RSRC, EX_MEM_RDST}), .in_1(NOP_2), .out(multiplexer_5_out));  // open: sel
  Register #(.Bits(16)) Mem_Wb (.D(multiplexer_5_out), .C(clk));  // open: en, Q
  // Pins of 1 and 4 bits meet at IF_ID_RDST
  // Pins of 1 and 4 bits meet at IF_ID_RSRC
  // Pins of 1 and 4 bits meet at ID_EX_RDST
  // Pins of 1 and 8 bits meet at ID_Ex_q
  // Pins of 1 and 2 bits meet at ID_EX_WR_MODE
  // Pins of 1 and 4 bits meet at EX_MEM_RDST
  // Pins of 1 and 2 bits meet at EX_MEM_WR_MODE
  // Pins of 1 and 2 bits meet at 2'b10
  // Pins of 1 and 2 bits meet at 2'b00
  // Pins of 1 and 15 bits meet at multiplexer_3_out
  // Pins of 1 and 15 bits meet at add_1_s
endmodule
